// Logisim project project.circ as structural Verilog: 5 circuits, main circuit main
// rising
module main (
);

  wire and_1_out, and_2_out, and_3_out, and_4_out, and_5_out, and_6_out, and_7_out, and_8_out, and_9_out,
       button_1_out, button_2_out, button_3_out, button_4_out, cdm_16_1_p3, cdm_16_1_p5, cdm_16_1_p6,
       cdm_16_1_p7, clk, comparator_1_eq, comparator_2_eq, comparator_3_eq, comparator_4_eq, comparator_5_eq,
       d_ff_1_qn, demultiplexer_1_out0, demultiplexer_1_out1, demultiplexer_1_out2, demultiplexer_1_out4,
       interrupt_arbiter_1_iack_2, interrupt_arbiter_1_irq_out, jIAck, jIRQ, menu_1_term_clock,
       menu_1_term_enable, not_1_out, or_1_out, priority_encoder_1_gs, s_r_ff_1_q, stable_clock_1_p2;
  wire [1:0] joystick_1_x, joystick_1_y;
  wire [2:0] priority_encoder_1_out;
  wire [4:0] row_q;
  wire [5:0] interrupt_arbiter_1_vec_out, menu_1_cursor_col;
  wire [6:0] menu_1_term_data;
  wire [15:0] cdm_16_1_p8, cdm_16_1_p9, cdm_16_1_p10, controlled_buffer_1_out, cursor_q, hi_q, joy, lo_q;
  wire [31:0] video_adapter_1_o1, video_adapter_1_o2, video_adapter_1_o3, video_adapter_1_o4,
       video_adapter_1_o5, video_adapter_1_o6, video_adapter_1_o7, video_adapter_1_o8, video_adapter_1_o9,
       video_adapter_1_o10, video_adapter_1_o11, video_adapter_1_o12, video_adapter_1_o13,
       video_adapter_1_o14, video_adapter_1_o15, video_adapter_1_o16, video_adapter_1_o17,
       video_adapter_1_o18, video_adapter_1_o19, video_adapter_1_o20, video_adapter_1_o21,
       video_adapter_1_o22, video_adapter_1_o23, video_adapter_1_o24, video_adapter_1_o25,
       video_adapter_1_o26, video_adapter_1_o27, video_adapter_1_o28, video_adapter_1_o29,
       video_adapter_1_o30, video_adapter_1_o31, video_adapter_1_o32;

  // stable_clock stable_clock_1: pin names not known; wires that end beside it: clk, stable_clock_1_p2
  D_Flip_Flop #(.trigger("falling")) d_ff_1 (
    .clk(clk), .D(stable_clock_1_p2), .Qn(d_ff_1_qn));  // open: Q, preset, en, reset
  and and_1 (and_1_out, stable_clock_1_p2, d_ff_1_qn);
  S_R_Flip_Flop #(.trigger("falling")) s_r_ff_1 (
    .S(and_1_out), .clk(clk), .R(interrupt_arbiter_1_iack_2), .Q(s_r_ff_1_q));  // open: Qn, preset, reset, en
  interrupt_arbiter interrupt_arbiter_1 (
    .IRQ_2(s_r_ff_1_q), .vec_2(6'b000110), .IAck_2(interrupt_arbiter_1_iack_2),
    .IRQ_out(interrupt_arbiter_1_irq_out), .vec_out(interrupt_arbiter_1_vec_out), .IAck_out(cdm_16_1_p3),
    .IRQ_1(jIRQ), .vec_1(6'b000101), .IAck_1(jIAck), .clk(clk));
  Clock clock_1 (.out(clk));
  // CdM_16 cdm_16_1: pin names not known; wires that end beside it: interrupt_arbiter_1_irq_out, interrupt_arbiter_1_vec_out, cdm_16_1_p3, clk, cdm_16_1_p5, cdm_16_1_p6, cdm_16_1_p7, cdm_16_1_p8, cdm_16_1_p9, cdm_16_1_p10
  Comparator #(.width(16), .mode("unsigned")) comparator_1 (
    .a(16'h82), .b(cdm_16_1_p8), .eq(comparator_1_eq));  // open: gt, lt
  Comparator #(.width(16), .mode("unsigned")) comparator_2 (
    .a(16'h80), .b(cdm_16_1_p8), .eq(comparator_2_eq));  // open: gt, lt
  Comparator #(.width(16), .mode("unsigned")) comparator_3 (
    .a(16'h84), .b(cdm_16_1_p8), .eq(comparator_3_eq));  // open: gt, lt
  Comparator #(.width(16), .mode("unsigned")) comparator_4 (
    .a(16'h85), .b(cdm_16_1_p8), .eq(comparator_4_eq));  // open: gt, lt
  Comparator #(.width(16), .mode("unsigned")) comparator_5 (
    .a(16'h86), .b(cdm_16_1_p8), .eq(comparator_5_eq));  // open: gt, lt
  and and_2 (and_2_out, ~priority_encoder_1_gs, cdm_16_1_p5);  // AND_Gate
  and and_3 (and_3_out, comparator_1_eq, cdm_16_1_p5);
  and and_4 (and_4_out, comparator_2_eq, cdm_16_1_p5);
  and and_5 (and_5_out, comparator_3_eq, cdm_16_1_p5);
  and and_6 (and_6_out, comparator_4_eq, cdm_16_1_p5);
  and and_7 (and_7_out, comparator_5_eq, cdm_16_1_p5);
  not not_1 (not_1_out, cdm_16_1_p6);
  assign controlled_buffer_1_out = not_1_out ? cdm_16_1_p9 : 16'bz;  // Controlled_Buffer controlled_buffer_1
  assign cdm_16_1_p10 = cdm_16_1_p6 ? controlled_buffer_1_out : 16'bz;  // Controlled_Buffer controlled_buffer_2
  Priority_Encoder priority_encoder_1 (
    .in0(and_3_out), .in1(and_4_out), .in2(and_5_out), .in3(and_6_out), .in4(and_7_out),
    .out(priority_encoder_1_out), .gs(priority_encoder_1_gs));  // open: in5, in6, in7, en_in, en_out
  // RAM ram_1: pin names not known; wires that end beside it: cdm_16_1_p8, cdm_16_1_p7, and_2_out, clk, cdm_16_1_p6, controlled_buffer_1_out
  Multiplexer #(.select(3), .width(16)) multiplexer_1 (
    .in3(joy), .out(controlled_buffer_1_out), .sel(priority_encoder_1_out), .en(and_8_out));  // open: in0, in1, in2, in4, in5, in6, in7
  and and_8 (and_8_out, priority_encoder_1_gs, cdm_16_1_p5, cdm_16_1_p6);
  Demultiplexer #(.select(3), .disabled(0)) demultiplexer_1 (
    .out0(demultiplexer_1_out0), .out1(demultiplexer_1_out1), .out2(demultiplexer_1_out2),
    .out4(demultiplexer_1_out4), .in(1'b1), .sel(priority_encoder_1_out), .en(and_9_out));  // open: out3, out5, out6, out7
  and and_9 (and_9_out, priority_encoder_1_gs, cdm_16_1_p5, ~cdm_16_1_p6);  // AND_Gate
  Register #(.width(16)) lo (.D(controlled_buffer_1_out), .en(demultiplexer_1_out0), .Q(lo_q), .clk(clk));  // open: clr
  Register #(.width(16)) hi (.D(controlled_buffer_1_out), .en(demultiplexer_1_out1), .Q(hi_q), .clk(clk));  // open: clr
  Register #(.width(5)) row (
    .D(controlled_buffer_1_out[4:0]), .en(demultiplexer_1_out2), .Q(row_q), .clk(clk));  // open: clr
  or or_1 (or_1_out, demultiplexer_1_out1, demultiplexer_1_out0);
  Register #(.width(16)) cursor (
    .D(controlled_buffer_1_out), .en(demultiplexer_1_out4), .Q(cursor_q), .clk(clk));  // open: clr
  video_adapter video_adapter_1 (
    .cursor(cursor_q), .low(lo_q), .hi(hi_q), .row(row_q), .enable(or_1_out), .clock(clk),
    .o1(video_adapter_1_o1), .o2(video_adapter_1_o2), .o3(video_adapter_1_o3), .o4(video_adapter_1_o4),
    .o5(video_adapter_1_o5), .o6(video_adapter_1_o6), .o7(video_adapter_1_o7), .o8(video_adapter_1_o8),
    .o9(video_adapter_1_o9), .o10(video_adapter_1_o10), .o11(video_adapter_1_o11), .o12(video_adapter_1_o12),
    .o13(video_adapter_1_o13), .o14(video_adapter_1_o14), .o15(video_adapter_1_o15),
    .o16(video_adapter_1_o16), .o17(video_adapter_1_o17), .o18(video_adapter_1_o18),
    .o19(video_adapter_1_o19), .o20(video_adapter_1_o20), .o21(video_adapter_1_o21),
    .o22(video_adapter_1_o22), .o23(video_adapter_1_o23), .o24(video_adapter_1_o24),
    .o25(video_adapter_1_o25), .o26(video_adapter_1_o26), .o27(video_adapter_1_o27),
    .o28(video_adapter_1_o28), .o29(video_adapter_1_o29), .o30(video_adapter_1_o30),
    .o31(video_adapter_1_o31), .o32(video_adapter_1_o32));
  DotMatrix #(.inputtype("row"), .matrixcols(32), .matrixrows(32)) dotmatrix_1 (
    .row0(video_adapter_1_o1), .row1(video_adapter_1_o2), .row2(video_adapter_1_o3),
    .row3(video_adapter_1_o4), .row4(video_adapter_1_o5), .row5(video_adapter_1_o6),
    .row6(video_adapter_1_o7), .row7(video_adapter_1_o8), .row8(video_adapter_1_o9),
    .row9(video_adapter_1_o10), .row10(video_adapter_1_o11), .row11(video_adapter_1_o12),
    .row12(video_adapter_1_o13), .row13(video_adapter_1_o14), .row14(video_adapter_1_o15),
    .row15(video_adapter_1_o16), .row16(video_adapter_1_o17), .row17(video_adapter_1_o18),
    .row18(video_adapter_1_o19), .row19(video_adapter_1_o20), .row20(video_adapter_1_o21),
    .row21(video_adapter_1_o22), .row22(video_adapter_1_o23), .row23(video_adapter_1_o24),
    .row24(video_adapter_1_o25), .row25(video_adapter_1_o26), .row26(video_adapter_1_o27),
    .row27(video_adapter_1_o28), .row28(video_adapter_1_o29), .row29(video_adapter_1_o30),
    .row30(video_adapter_1_o31), .row31(video_adapter_1_o32));
  TTY #(.rows(3), .cols(16), .trigger("falling")) tty_1 (
    .data(menu_1_term_data), .clk(menu_1_term_clock), .we(menu_1_term_enable));  // open: clr
  DotMatrix #(.matrixcols(1), .matrixrows(6)) dotmatrix_2 (.col0(menu_1_cursor_col));
  menu menu_1 (
    .cursor_col(menu_1_cursor_col), .term_data(menu_1_term_data), .term_clock(menu_1_term_clock),
    .term_enable(menu_1_term_enable), .clock(clk));  // open: cursor, data
  Button button_1 (.out(button_1_out));
  Joystick #(.bits(2)) joystick_1 (.x(joystick_1_x), .y(joystick_1_y));
  gamepad gamepad_1 (
    .data(joy), .joy({joystick_1_y, joystick_1_x}), .B(button_3_out), .A(button_4_out), .R(button_2_out),
    .IAck(jIAck), .clk(clk), .IRQ(jIRQ), .L(button_1_out));
  Button button_2 (.out(button_2_out));
  Button button_3 (.out(button_3_out));
  Button button_4 (.out(button_4_out));
endmodule

module interrupt_arbiter (
  input  IRQ_2,
  input  [5:0] vec_2,
  input  IAck_out,
  input  IRQ_1,
  input  [5:0] vec_1,
  input  clk,
  output IRQ_out,
  output [5:0] vec_out,
  output IAck_2,
  output IAck_1
);

  wire and_2_out, and_3_out, and_4_out, and_5_out, and_7_out, and_8_out, d_ff_1_q, d_ff_2_q, or_1_out,
       or_2_out;

  and and_1 (IAck_2, d_ff_1_q, IAck_out);
  and and_2 (and_2_out, IRQ_2, ~IRQ_1, ~d_ff_2_q);  // AND_Gate
  and and_3 (and_3_out, d_ff_1_q, IAck_out);
  and and_4 (and_4_out, ~d_ff_1_q, IRQ_1);  // AND_Gate
  and and_5 (and_5_out, d_ff_2_q, IAck_out);
  and and_6 (IAck_1, IAck_out, d_ff_2_q);
  or or_1 (or_1_out, and_2_out, and_3_out);
  or or_2 (or_2_out, and_4_out, and_5_out);
  D_Flip_Flop d_ff_1 (.clk(clk), .D(or_1_out), .Q(d_ff_1_q));  // open: Qn, preset, en, reset
  D_Flip_Flop d_ff_2 (.clk(clk), .D(or_2_out), .Q(d_ff_2_q));  // open: Qn, preset, en, reset
  and and_7 (and_7_out, d_ff_1_q, IAck_out);
  assign vec_out = and_7_out ? vec_2 : 6'bz;  // Controlled_Buffer controlled_buffer_1
  and and_8 (and_8_out, d_ff_2_q, IAck_out);
  assign vec_out = and_8_out ? vec_1 : 6'bz;  // Controlled_Buffer controlled_buffer_2
  Pull_Resistor pull_resistor_1 (.node(IRQ_out));
  assign IRQ_out = d_ff_1_q ? IRQ_2 : 1'bz;  // Controlled_Buffer controlled_buffer_3
  assign IRQ_out = d_ff_2_q ? IRQ_1 : 1'bz;  // Controlled_Buffer controlled_buffer_4
endmodule

module gamepad (
  input  IAck,
  input  clk,
  input  [3:0] joy,
  input  R,
  input  L,
  input  B,
  input  A,
  output [15:0] data,
  output IRQ
);

  wire and_5_out, comparator_1_eq;
  wire [5:2] and_3_out;
  wire [15:0] register_1_q;

  and and_1 (and_3_out[4], joy[0], joy[1]);
  and and_2 (and_3_out[5], joy[0], ~joy[1]);  // AND_Gate
  and and_3 (and_3_out[2], joy[2], joy[3]);
  and and_4 (and_3_out[3], joy[2], ~joy[3]);  // AND_Gate
  and and_5 (and_5_out, ~IAck, comparator_1_eq);  // AND_Gate
  Register #(.width(16)) register_1 (
    .D({{8{1'b0}}, L, R, and_3_out, B, A}), .en(and_5_out), .Q(register_1_q), .clk(clk));  // open: clr
  Register #(.width(16), .trigger("falling")) register_2 (
    .D(register_1_q), .en(IAck), .Q(data), .clk(clk));  // open: clr
  Comparator #(.width(16), .mode("unsigned")) comparator_1 (
    .a(data), .b(register_1_q), .eq(comparator_1_eq));  // open: gt, lt
  not not_1 (IRQ, comparator_1_eq);
endmodule

module video_adapter (
  input  [15:0] cursor,
  input  [15:0] low,
  input  [15:0] hi,
  input  [4:0] row,
  input  enable,
  input  clock,
  output [31:0] o1,
  output [31:0] o2,
  output [31:0] o3,
  output [31:0] o4,
  output [31:0] o5,
  output [31:0] o6,
  output [31:0] o7,
  output [31:0] o8,
  output [31:0] o9,
  output [31:0] o10,
  output [31:0] o11,
  output [31:0] o12,
  output [31:0] o13,
  output [31:0] o14,
  output [31:0] o15,
  output [31:0] o16,
  output [31:0] o17,
  output [31:0] o18,
  output [31:0] o19,
  output [31:0] o20,
  output [31:0] o21,
  output [31:0] o22,
  output [31:0] o23,
  output [31:0] o24,
  output [31:0] o25,
  output [31:0] o26,
  output [31:0] o27,
  output [31:0] o28,
  output [31:0] o29,
  output [31:0] o30,
  output [31:0] o31,
  output [31:0] o32
);

  wire and_1_out, demultiplexer_1_out0, demultiplexer_1_out1, demultiplexer_1_out2, demultiplexer_1_out3,
       demultiplexer_1_out4, demultiplexer_1_out5, demultiplexer_1_out6, demultiplexer_1_out7,
       demultiplexer_1_out8, demultiplexer_1_out9, demultiplexer_1_out10, demultiplexer_1_out11,
       demultiplexer_1_out12, demultiplexer_1_out13, demultiplexer_1_out14, demultiplexer_1_out15,
       demultiplexer_1_out16, demultiplexer_1_out17, demultiplexer_1_out18, demultiplexer_1_out19,
       demultiplexer_1_out20, demultiplexer_1_out21, demultiplexer_1_out22, demultiplexer_1_out23,
       demultiplexer_1_out24, demultiplexer_1_out25, demultiplexer_1_out26, demultiplexer_1_out27,
       demultiplexer_1_out28, demultiplexer_1_out29, demultiplexer_1_out30, demultiplexer_1_out31,
       demultiplexer_2_out0, demultiplexer_2_out1, demultiplexer_2_out2, demultiplexer_2_out3,
       demultiplexer_2_out4, demultiplexer_2_out5, demultiplexer_2_out6, demultiplexer_2_out7,
       demultiplexer_2_out8, demultiplexer_2_out9, demultiplexer_2_out10, demultiplexer_2_out11,
       demultiplexer_2_out12, demultiplexer_2_out13, demultiplexer_2_out14, demultiplexer_2_out15,
       demultiplexer_2_out16, demultiplexer_2_out17, demultiplexer_2_out18, demultiplexer_2_out19,
       demultiplexer_2_out20, demultiplexer_2_out21, demultiplexer_2_out22, demultiplexer_2_out23,
       demultiplexer_2_out24, demultiplexer_2_out25, demultiplexer_2_out26, demultiplexer_2_out27,
       demultiplexer_2_out28, demultiplexer_2_out29, demultiplexer_2_out30, demultiplexer_2_out31, not_1_out,
       pull_resistor_1_node, stable_clock_1_p1, stable_clock_1_p3;
  wire [15:0] register_33_q, register_34_q;
  wire [31:0] demultiplexer_3_out31;

  Demultiplexer #(.select(5), .disabled(0)) demultiplexer_1 (
    .out0(demultiplexer_1_out0), .out1(demultiplexer_1_out1), .out2(demultiplexer_1_out2),
    .out3(demultiplexer_1_out3), .out4(demultiplexer_1_out4), .out5(demultiplexer_1_out5),
    .out6(demultiplexer_1_out6), .out7(demultiplexer_1_out7), .out8(demultiplexer_1_out8),
    .out9(demultiplexer_1_out9), .out10(demultiplexer_1_out10), .out11(demultiplexer_1_out11),
    .out12(demultiplexer_1_out12), .out13(demultiplexer_1_out13), .out14(demultiplexer_1_out14),
    .out15(demultiplexer_1_out15), .out16(demultiplexer_1_out16), .out17(demultiplexer_1_out17),
    .out18(demultiplexer_1_out18), .out19(demultiplexer_1_out19), .out20(demultiplexer_1_out20),
    .out21(demultiplexer_1_out21), .out22(demultiplexer_1_out22), .out23(demultiplexer_1_out23),
    .out24(demultiplexer_1_out24), .out25(demultiplexer_1_out25), .out26(demultiplexer_1_out26),
    .out27(demultiplexer_1_out27), .out28(demultiplexer_1_out28), .out29(demultiplexer_1_out29),
    .out30(demultiplexer_1_out30), .out31(demultiplexer_1_out31), .in(1'b1), .sel(row), .en(enable));
  Register #(.width(32), .trigger("falling")) register_1 (
    .D({hi, low}), .en(demultiplexer_1_out0), .Q(o1), .clk(clock));  // open: clr
  Register #(.width(32), .trigger("falling")) register_2 (
    .D({hi, low}), .en(demultiplexer_1_out1), .Q(o2), .clk(clock));  // open: clr
  Register #(.width(32), .trigger("falling")) register_3 (
    .D({hi, low}), .en(demultiplexer_1_out2), .Q(o3), .clk(clock));  // open: clr
  Register #(.width(32), .trigger("falling")) register_4 (
    .D({hi, low}), .en(demultiplexer_1_out3), .Q(o4), .clk(clock));  // open: clr
  Register #(.width(32), .trigger("falling")) register_5 (
    .D({hi, low}), .en(demultiplexer_1_out4), .Q(o5), .clk(clock));  // open: clr
  Register #(.width(32), .trigger("falling")) register_6 (
    .D({hi, low}), .en(demultiplexer_1_out5), .Q(o6), .clk(clock));  // open: clr
  Register #(.width(32), .trigger("falling")) register_7 (
    .D({hi, low}), .en(demultiplexer_1_out6), .Q(o7), .clk(clock));  // open: clr
  Register #(.width(32), .trigger("falling")) register_8 (
    .D({hi, low}), .en(demultiplexer_1_out7), .Q(o8), .clk(clock));  // open: clr
  Register #(.width(32), .trigger("falling")) register_9 (
    .D({hi, low}), .en(demultiplexer_1_out8), .Q(o9), .clk(clock));  // open: clr
  Register #(.width(32), .trigger("falling")) register_10 (
    .D({hi, low}), .en(demultiplexer_1_out9), .Q(o10), .clk(clock));  // open: clr
  Register #(.width(32), .trigger("falling")) register_11 (
    .D({hi, low}), .en(demultiplexer_1_out10), .Q(o11), .clk(clock));  // open: clr
  Register #(.width(32), .trigger("falling")) register_12 (
    .D({hi, low}), .en(demultiplexer_1_out11), .Q(o12), .clk(clock));  // open: clr
  Register #(.width(32), .trigger("falling")) register_13 (
    .D({hi, low}), .en(demultiplexer_1_out12), .Q(o13), .clk(clock));  // open: clr
  Register #(.width(32), .trigger("falling")) register_14 (
    .D({hi, low}), .en(demultiplexer_1_out13), .Q(o14), .clk(clock));  // open: clr
  Register #(.width(32), .trigger("falling")) register_15 (
    .D({hi, low}), .en(demultiplexer_1_out14), .Q(o15), .clk(clock));  // open: clr
  Register #(.width(32), .trigger("falling")) register_16 (
    .D({hi, low}), .en(demultiplexer_1_out15), .Q(o16), .clk(clock));  // open: clr
  Register #(.width(32), .trigger("falling")) register_17 (
    .D({hi, low}), .en(demultiplexer_1_out16), .Q(o17), .clk(clock));  // open: clr
  Register #(.width(32), .trigger("falling")) register_18 (
    .D({hi, low}), .en(demultiplexer_1_out17), .Q(o18), .clk(clock));  // open: clr
  Register #(.width(32), .trigger("falling")) register_19 (
    .D({hi, low}), .en(demultiplexer_1_out18), .Q(o19), .clk(clock));  // open: clr
  Register #(.width(32), .trigger("falling")) register_20 (
    .D({hi, low}), .en(demultiplexer_1_out19), .Q(o20), .clk(clock));  // open: clr
  Register #(.width(32), .trigger("falling")) register_21 (
    .D({hi, low}), .en(demultiplexer_1_out20), .Q(o21), .clk(clock));  // open: clr
  Register #(.width(32), .trigger("falling")) register_22 (
    .D({hi, low}), .en(demultiplexer_1_out21), .Q(o22), .clk(clock));  // open: clr
  Register #(.width(32), .trigger("falling")) register_23 (
    .D({hi, low}), .en(demultiplexer_1_out22), .Q(o23), .clk(clock));  // open: clr
  Register #(.width(32), .trigger("falling")) register_24 (
    .D({hi, low}), .en(demultiplexer_1_out23), .Q(o24), .clk(clock));  // open: clr
  Register #(.width(32), .trigger("falling")) register_25 (
    .D({hi, low}), .en(demultiplexer_1_out24), .Q(o25), .clk(clock));  // open: clr
  Register #(.width(32), .trigger("falling")) register_26 (
    .D({hi, low}), .en(demultiplexer_1_out25), .Q(o26), .clk(clock));  // open: clr
  Register #(.width(32), .trigger("falling")) register_27 (
    .D({hi, low}), .en(demultiplexer_1_out26), .Q(o27), .clk(clock));  // open: clr
  Register #(.width(32), .trigger("falling")) register_28 (
    .D({hi, low}), .en(demultiplexer_1_out27), .Q(o28), .clk(clock));  // open: clr
  Register #(.width(32), .trigger("falling")) register_29 (
    .D({hi, low}), .en(demultiplexer_1_out28), .Q(o29), .clk(clock));  // open: clr
  Register #(.width(32), .trigger("falling")) register_30 (
    .D({hi, low}), .en(demultiplexer_1_out29), .Q(o30), .clk(clock));  // open: clr
  Register #(.width(32), .trigger("falling")) register_31 (
    .D({hi, low}), .en(demultiplexer_1_out30), .Q(o31), .clk(clock));  // open: clr
  Register #(.width(32), .trigger("falling")) register_32 (
    .D({hi, low}), .en(demultiplexer_1_out31), .Q(o32), .clk(clock));  // open: clr
  assign o2 = demultiplexer_2_out1 ? demultiplexer_3_out31 : 32'bz;  // Controlled_Buffer controlled_buffer_1
  assign o1 = demultiplexer_2_out0 ? demultiplexer_3_out31 : 32'bz;  // Controlled_Buffer controlled_buffer_2
  Demultiplexer #(.select(5), .enable("false")) demultiplexer_2 (
    .out0(demultiplexer_2_out0), .out1(demultiplexer_2_out1), .out2(demultiplexer_2_out2),
    .out3(demultiplexer_2_out3), .out4(demultiplexer_2_out4), .out5(demultiplexer_2_out5),
    .out6(demultiplexer_2_out6), .out7(demultiplexer_2_out7), .out8(demultiplexer_2_out8),
    .out9(demultiplexer_2_out9), .out10(demultiplexer_2_out10), .out11(demultiplexer_2_out11),
    .out12(demultiplexer_2_out12), .out13(demultiplexer_2_out13), .out14(demultiplexer_2_out14),
    .out15(demultiplexer_2_out15), .out16(demultiplexer_2_out16), .out17(demultiplexer_2_out17),
    .out18(demultiplexer_2_out18), .out19(demultiplexer_2_out19), .out20(demultiplexer_2_out20),
    .out21(demultiplexer_2_out21), .out22(demultiplexer_2_out22), .out23(demultiplexer_2_out23),
    .out24(demultiplexer_2_out24), .out25(demultiplexer_2_out25), .out26(demultiplexer_2_out26),
    .out27(demultiplexer_2_out27), .out28(demultiplexer_2_out28), .out29(demultiplexer_2_out29),
    .out30(demultiplexer_2_out30), .out31(demultiplexer_2_out31), .in(1'b1), .sel(cursor[9:5]));
  assign o3 = demultiplexer_2_out2 ? demultiplexer_3_out31 : 32'bz;  // Controlled_Buffer controlled_buffer_3
  assign o4 = demultiplexer_2_out3 ? demultiplexer_3_out31 : 32'bz;  // Controlled_Buffer controlled_buffer_4
  assign o6 = demultiplexer_2_out5 ? demultiplexer_3_out31 : 32'bz;  // Controlled_Buffer controlled_buffer_5
  assign o5 = demultiplexer_2_out4 ? demultiplexer_3_out31 : 32'bz;  // Controlled_Buffer controlled_buffer_6
  assign o7 = demultiplexer_2_out6 ? demultiplexer_3_out31 : 32'bz;  // Controlled_Buffer controlled_buffer_7
  assign o8 = demultiplexer_2_out7 ? demultiplexer_3_out31 : 32'bz;  // Controlled_Buffer controlled_buffer_8
  assign o9 = demultiplexer_2_out8 ? demultiplexer_3_out31 : 32'bz;  // Controlled_Buffer controlled_buffer_9
  assign o10 = demultiplexer_2_out9 ? demultiplexer_3_out31 : 32'bz;  // Controlled_Buffer controlled_buffer_10
  assign o12 = demultiplexer_2_out11 ? demultiplexer_3_out31 : 32'bz;  // Controlled_Buffer controlled_buffer_11
  assign o11 = demultiplexer_2_out10 ? demultiplexer_3_out31 : 32'bz;  // Controlled_Buffer controlled_buffer_12
  assign o14 = demultiplexer_2_out13 ? demultiplexer_3_out31 : 32'bz;  // Controlled_Buffer controlled_buffer_13
  assign o13 = demultiplexer_2_out12 ? demultiplexer_3_out31 : 32'bz;  // Controlled_Buffer controlled_buffer_14
  assign o16 = demultiplexer_2_out15 ? demultiplexer_3_out31 : 32'bz;  // Controlled_Buffer controlled_buffer_15
  assign o15 = demultiplexer_2_out14 ? demultiplexer_3_out31 : 32'bz;  // Controlled_Buffer controlled_buffer_16
  assign o17 = demultiplexer_2_out16 ? demultiplexer_3_out31 : 32'bz;  // Controlled_Buffer controlled_buffer_17
  assign o18 = demultiplexer_2_out17 ? demultiplexer_3_out31 : 32'bz;  // Controlled_Buffer controlled_buffer_18
  assign o20 = demultiplexer_2_out19 ? demultiplexer_3_out31 : 32'bz;  // Controlled_Buffer controlled_buffer_19
  assign o19 = demultiplexer_2_out18 ? demultiplexer_3_out31 : 32'bz;  // Controlled_Buffer controlled_buffer_20
  assign o21 = demultiplexer_2_out20 ? demultiplexer_3_out31 : 32'bz;  // Controlled_Buffer controlled_buffer_21
  assign o22 = demultiplexer_2_out21 ? demultiplexer_3_out31 : 32'bz;  // Controlled_Buffer controlled_buffer_22
  assign o24 = demultiplexer_2_out23 ? demultiplexer_3_out31 : 32'bz;  // Controlled_Buffer controlled_buffer_23
  assign o23 = demultiplexer_2_out22 ? demultiplexer_3_out31 : 32'bz;  // Controlled_Buffer controlled_buffer_24
  Register #(.width(16)) register_33 (.D(cursor), .Q(register_33_q), .clk(clock));  // open: en, clr
  Register #(.width(16), .trigger("falling")) register_34 (
    .D(cursor), .Q(register_34_q), .clk(clock));  // open: en, clr
  assign o25 = demultiplexer_2_out24 ? demultiplexer_3_out31 : 32'bz;  // Controlled_Buffer controlled_buffer_25
  assign o26 = demultiplexer_2_out25 ? demultiplexer_3_out31 : 32'bz;  // Controlled_Buffer controlled_buffer_26
  // stable_clock stable_clock_1: pin names not known; wires that end beside it: stable_clock_1_p1, clock, stable_clock_1_p3
  Comparator #(.width(16)) comparator_1 (.a(register_33_q), .b(register_34_q), .eq(stable_clock_1_p1));  // open: gt, lt
  assign o28 = demultiplexer_2_out27 ? demultiplexer_3_out31 : 32'bz;  // Controlled_Buffer controlled_buffer_27
  assign o27 = demultiplexer_2_out26 ? demultiplexer_3_out31 : 32'bz;  // Controlled_Buffer controlled_buffer_28
  not not_1 (not_1_out, stable_clock_1_p3);
  assign o30 = demultiplexer_2_out29 ? demultiplexer_3_out31 : 32'bz;  // Controlled_Buffer controlled_buffer_29
  assign o29 = demultiplexer_2_out28 ? demultiplexer_3_out31 : 32'bz;  // Controlled_Buffer controlled_buffer_30
  assign o31 = demultiplexer_2_out30 ? demultiplexer_3_out31 : 32'bz;  // Controlled_Buffer controlled_buffer_31
  assign o32 = demultiplexer_2_out31 ? demultiplexer_3_out31 : 32'bz;  // Controlled_Buffer controlled_buffer_32
  and and_1 (and_1_out, ~cursor[15], not_1_out);  // AND_Gate
  Demultiplexer #(.select(5), .tristate("true")) demultiplexer_3 (
    .out0(demultiplexer_3_out31[31]), .out1(demultiplexer_3_out31[30]), .out2(demultiplexer_3_out31[29]),
    .out3(demultiplexer_3_out31[28]), .out4(demultiplexer_3_out31[27]), .out5(demultiplexer_3_out31[26]),
    .out6(demultiplexer_3_out31[25]), .out7(demultiplexer_3_out31[24]), .out8(demultiplexer_3_out31[23]),
    .out9(demultiplexer_3_out31[22]), .out10(demultiplexer_3_out31[21]), .out11(demultiplexer_3_out31[20]),
    .out12(demultiplexer_3_out31[19]), .out13(demultiplexer_3_out31[18]), .out14(demultiplexer_3_out31[17]),
    .out15(demultiplexer_3_out31[16]), .out16(demultiplexer_3_out31[15]), .out17(demultiplexer_3_out31[14]),
    .out18(demultiplexer_3_out31[13]), .out19(demultiplexer_3_out31[12]), .out20(demultiplexer_3_out31[11]),
    .out21(demultiplexer_3_out31[10]), .out22(demultiplexer_3_out31[9]), .out23(demultiplexer_3_out31[8]),
    .out24(demultiplexer_3_out31[7]), .out25(demultiplexer_3_out31[6]), .out26(demultiplexer_3_out31[5]),
    .out27(demultiplexer_3_out31[4]), .out28(demultiplexer_3_out31[3]), .out29(demultiplexer_3_out31[2]),
    .out30(demultiplexer_3_out31[1]), .out31(demultiplexer_3_out31[0]), .in(pull_resistor_1_node),
    .sel(cursor[4:0]), .en(and_1_out));
  Pull_Resistor #(.pull("X")) pull_resistor_1 (.node(pull_resistor_1_node));

  // Other names for the same wires on the sheet: clk = clock
endmodule

module menu (
  input  [7:0] cursor,
  input  [7:0] data,
  input  clock,
  output [5:0] cursor_col,
  output term_enable,
  output term_clock,
  output [6:0] term_data
);

  wire Char_counter_carry, comparator_1_eq, comparator_2_eq, nor_2_out, s_r_ff_1_qn, stable_clock_1_p1,
       stable_clock_1_p3;
  wire [5:0] Char_counter_q;
  wire [7:0] adder_1_out, multiplexer_1_out, multiplexer_2_out, multiplexer_3_out, multiplexer_4_out,
       register_1_q, register_2_q, register_3_q, register_4_q;

  Register register_1 (.D(cursor), .Q(register_1_q), .clk(clock));  // open: en, clr
  Register #(.trigger("falling")) register_2 (.D(cursor), .Q(register_2_q), .clk(clock));  // open: en, clr
  Comparator comparator_1 (.a(register_1_q), .b(register_2_q), .eq(comparator_1_eq));  // open: gt, lt
  Multiplexer #(.select(2), .width(8), .disabled(0), .enable("false")) multiplexer_1 (
    .in0(8'h18), .in1(8'h20), .in2(8'h28), .in3(8'h30), .out(multiplexer_1_out), .sel(register_3_q[1:0]));
  Multiplexer #(.width(8), .disabled(0), .enable("false")) multiplexer_2 (
    .in0(8'h38), .in1(8'h40), .out(multiplexer_2_out), .sel(register_3_q[2]));
  Counter #(.width(6), .max('h2f), .trigger("falling")) Char_counter (
    .count(term_enable), .Q(Char_counter_q), .carry(Char_counter_carry), .clk(clock));  // open: load, D, clr
  Register register_3 (.D(data), .en(comparator_2_eq), .Q(register_3_q), .clk(clock));  // open: clr
  // stable_clock stable_clock_1: pin names not known; wires that end beside it: stable_clock_1_p1, clock, stable_clock_1_p3
  nor nor_1 (stable_clock_1_p1, cursor[7], ~comparator_1_eq);  // NOR_Gate
  Multiplexer #(.width(8), .disabled(0), .enable("false")) multiplexer_3 (
    .in0(8'h48), .in1(8'h50), .out(multiplexer_3_out), .sel(register_3_q[3]));
  Register #(.trigger("falling")) register_4 (
    .D(register_3_q), .en(Char_counter_carry), .Q(register_4_q), .clk(clock));  // open: clr
  Demultiplexer #(.select(2), .disabled(0), .enable("false")) demultiplexer_1 (
    .out0(cursor_col[4]), .out1(cursor_col[2]), .out2(cursor_col[0]), .in(nor_2_out), .sel(cursor[1:0]));  // open: out3
  nor nor_2 (nor_2_out, cursor[7], stable_clock_1_p3);
  Multiplexer #(.select(3), .width(8), .disabled(0), .enable("false")) multiplexer_4 (
    .in0({8{1'b0}}), .in1(multiplexer_1_out), .in2(8'h8), .in3(multiplexer_2_out), .in4(8'h10),
    .in5(multiplexer_3_out), .out(multiplexer_4_out), .sel(Char_counter_q[5:3]));  // open: in6, in7
  Comparator comparator_2 (.a(register_3_q), .b(register_4_q), .eq(comparator_2_eq));  // open: gt, lt
  Adder adder_1 (.a(multiplexer_4_out), .b({{5{1'b0}}, Char_counter_q[2:0]}), .out(adder_1_out));  // open: cin, cout
  S_R_Flip_Flop #(.trigger("falling")) s_r_ff_1 (
    .S(Char_counter_carry), .clk(clock), .R(1'b0), .Qn(s_r_ff_1_qn));  // open: Q, preset, reset, en
  ROM #(.dataWidth(7)) rom_1 (.addr(adder_1_out), .data(term_data));  // open: sel
  or or_1 (term_enable, s_r_ff_1_qn, ~comparator_2_eq);  // OR_Gate

  assign {cursor_col[5], cursor_col[3], cursor_col[1]} = 3'b000;
  assign term_clock = clock;

  // Notes on the sheet:
  //   Detects changes in
  //   cursor position
  //   These select the offsets of the
  //   8-byte blocks stored in ROM
  //   negative position
  //   = cursor is hidden
  //   Detects changes in data
  //   Locks the current value
  //   until the screen is refreshed
  //   Forms the column with the
  //   blinking cursor
  //   Character block ROM
  //   Refreshes the screen
  //   once after a reset
  //   contents of rom_1 (hex, n*v repeats v):
  //   54 6f 6f 6c 3a 20 20 20 43 6f 6c 6f 72 3a 20 20 46 69 6c 6c 3a 20 20 20 50 69 78 65 6c 20 20 20 4c
  //   69 6e 65 4*20 52 65 63 74 4*20 45 6c 6c 69 70 73 65 20 42 6c 61 63 6b 20 20 20 47 72 65 65 6e 20 20
  //   20 4f 66 66 5*20 4f 6e 6*20
endmodule
